// Logisim project cpu.circ as structural Verilog: 4 circuits, main circuit main
module main (
);

  wire _0_out, _1_out, _2_out, _3_out, _4_out, _5_out, _6_out, _7_out, C_out, Clock_out, cpu_1_memory_rw,
       not_1_out, not_2_out;
  wire [7:0] controlled_buffer_2_out, cpu_1_memory_address, cpu_1_memory_out, cpu_1_output, ram_1_data,
       t_ff_1_q;

  not not_1 (not_1_out, Clock_out);
  RAM ram_1 (.addr(cpu_1_memory_address), .data(ram_1_data), .clk(not_1_out), .ld(cpu_1_memory_rw));  // open: sel, clr
  assign ram_1_data = not_2_out ? cpu_1_memory_out : 8'bz;  // Controlled_Buffer controlled_buffer_1
  not not_2 (not_2_out, cpu_1_memory_rw);
  assign controlled_buffer_2_out = cpu_1_memory_rw ? ram_1_data : 8'bz;  // Controlled_Buffer controlled_buffer_2
  CPU cpu_1 (
    .Input(t_ff_1_q), .Memory_Address(cpu_1_memory_address), .Output(cpu_1_output), .Clock(Clock_out),
    .Memory_Out(cpu_1_memory_out), .Memory_In(controlled_buffer_2_out), .Memory_RW(cpu_1_memory_rw));
  Clock Clock (.out(Clock_out));
  Hex_Digit_Display hex_digit_display_1 (.value(cpu_1_output[7:4]));  // open: dp
  Hex_Digit_Display hex_digit_display_2 (.value(t_ff_1_q[7:4]));  // open: dp
  Hex_Digit_Display hex_digit_display_3 (.value(cpu_1_output[3:0]));  // open: dp
  Hex_Digit_Display hex_digit_display_4 (.value(t_ff_1_q[3:0]));  // open: dp
  Button C (.out(C_out));
  Button _0 (.out(_0_out));
  Button _1 (.out(_1_out));
  Button _2 (.out(_2_out));
  Button _3 (.out(_3_out));
  Button _4 (.out(_4_out));
  Button _5 (.out(_5_out));
  Button _6 (.out(_6_out));
  Button _7 (.out(_7_out));
  T_Flip_Flop t_ff_1 (.clk(_0_out), .T(_0_out), .Q(t_ff_1_q[0]), .reset(C_out));  // open: Qn, preset, en
  T_Flip_Flop t_ff_2 (.clk(_1_out), .T(_1_out), .Q(t_ff_1_q[1]), .reset(C_out));  // open: Qn, preset, en
  T_Flip_Flop t_ff_3 (.clk(_2_out), .T(_2_out), .Q(t_ff_1_q[2]), .reset(C_out));  // open: Qn, preset, en
  T_Flip_Flop t_ff_4 (.clk(_3_out), .T(_3_out), .Q(t_ff_1_q[3]), .reset(C_out));  // open: Qn, preset, en
  T_Flip_Flop t_ff_5 (.clk(_4_out), .T(_4_out), .Q(t_ff_1_q[4]), .reset(C_out));  // open: Qn, preset, en
  T_Flip_Flop t_ff_6 (.clk(_5_out), .T(_5_out), .Q(t_ff_1_q[5]), .reset(C_out));  // open: Qn, preset, en
  T_Flip_Flop t_ff_7 (.clk(_6_out), .T(_6_out), .Q(t_ff_1_q[6]), .reset(C_out));  // open: Qn, preset, en
  T_Flip_Flop t_ff_8 (.clk(_7_out), .T(_7_out), .Q(t_ff_1_q[7]), .reset(C_out));  // open: Qn, preset, en

  // Notes on the sheet:
  //   RAM
  //   Output
  //   Input
endmodule

module Data_Path (
  input  Clock,
  input  Write_MAR,
  input  Memory_RW,
  input  [7:0] MBR_In,
  input  Write_MBR,
  input  Write_PC,
  input  Write_SP,
  input  Write_B,
  input  Write_A,
  input  [7:0] Switch_Input,
  input  Write_Buf,
  input  [2:0] B_Bus_Select,
  input  [3:0] F,
  input  Write_OUT,
  output [7:0] MAR_Out,
  output [7:0] MBR_Out,
  output Z_Out,
  output [7:0] OUT_Out
);

  wire alu_1_z, not_1_out;
  wire [7:0] A_q, alu_1_c, B_q, Buf_q, controlled_buffer_1_out, multiplexer_1_out, PC_q, SP_q;

  Register #(.trigger("falling")) MAR (.D(alu_1_c), .en(Write_MAR), .Q(MAR_Out), .clk(Clock));  // open: clr
  Register #(.trigger("falling")) PC (.D(alu_1_c), .en(Write_PC), .Q(PC_q), .clk(Clock));  // open: clr
  Register #(.trigger("falling")) SP (.D(alu_1_c), .en(Write_SP), .Q(SP_q), .clk(Clock));  // open: clr
  Register #(.trigger("falling")) B (.D(alu_1_c), .en(Write_B), .Q(B_q), .clk(Clock));  // open: clr
  Register #(.trigger("falling")) A (.D(alu_1_c), .en(Write_A), .Q(A_q), .clk(Clock));  // open: clr
  Register #(.trigger("falling")) Buf (.D(alu_1_c), .en(Write_Buf), .Q(Buf_q), .clk(Clock));  // open: clr
  Register #(.trigger("falling")) OUT (.D(alu_1_c), .en(Write_OUT), .Q(OUT_Out), .clk(Clock));  // open: clr
  assign controlled_buffer_1_out = Memory_RW ? MBR_In : 8'bz;  // Controlled_Buffer controlled_buffer_1
  not not_1 (not_1_out, Memory_RW);
  assign controlled_buffer_1_out = not_1_out ? alu_1_c : 8'bz;  // Controlled_Buffer controlled_buffer_2
  Register #(.width(1), .trigger("falling")) Z (.D(alu_1_z), .Q(Z_Out), .clk(Clock));  // open: en, clr
  Register #(.trigger("falling")) MBR (
    .D(controlled_buffer_1_out), .en(Write_MBR), .Q(MBR_Out), .clk(Clock));  // open: clr
  Multiplexer #(.select(3), .width(8), .disabled(0), .enable("false")) multiplexer_1 (
    .in0(A_q), .in1(B_q), .in2(SP_q), .in3(PC_q), .in4(MBR_Out), .in5(MAR_Out), .in6(Switch_Input),
    .out(multiplexer_1_out), .sel(B_Bus_Select));  // open: in7
  ALU alu_1 (.A(Buf_q), .B(multiplexer_1_out), .F(F), .C(alu_1_c), .Z(alu_1_z));

  // Notes on the sheet:
  //   A Bus
  //   C Bus
  //   B Bus
endmodule

module ALU (
  input  [7:0] A,
  input  [7:0] B,
  input  [3:0] F,
  output Z,
  output [7:0] C
);

  wire [7:0] adder_1_out, adder_2_out, adder_3_out, and_1_out, or_1_out, subtractor_1_out, subtractor_2_out;

  Hex_Digit_Display hex_digit_display_1 (.value(A[7:4]));  // open: dp
  Hex_Digit_Display hex_digit_display_2 (.value(B[7:4]));  // open: dp
  Hex_Digit_Display hex_digit_display_3 (.value(A[3:0]));  // open: dp
  Hex_Digit_Display hex_digit_display_4 (.value(B[3:0]));  // open: dp
  Adder adder_1 (.a(A), .b(8'h1), .out(adder_1_out));  // open: cin, cout
  Adder adder_2 (.a(B), .b(8'h1), .out(adder_2_out));  // open: cin, cout
  Adder adder_3 (.a(A), .b(B), .out(adder_3_out));  // open: cin, cout
  Subtractor subtractor_1 (.a(A), .b(B), .out(subtractor_1_out));  // open: bin, bout
  assign and_1_out = A & B;  // AND_Gate and_1, 8 bits wide
  assign or_1_out = A | B;  // OR_Gate or_1, 8 bits wide
  Subtractor subtractor_2 (.a(B), .b(8'h1), .out(subtractor_2_out));  // open: bin, bout
  Multiplexer #(.select(4), .width(8), .disabled(0), .enable("false")) multiplexer_1 (
    .in0(A), .in1(B), .in2(adder_1_out), .in3(adder_2_out), .in4(adder_3_out), .in5(subtractor_1_out),
    .in6(and_1_out), .in7(or_1_out), .in8(subtractor_2_out), .out(C), .sel(F));  // open: in9, in10, in11, in12, in13, in14, in15
  Comparator comparator_1 (.a({8{1'b0}}), .b(C), .eq(Z));  // open: gt, lt
  Hex_Digit_Display hex_digit_display_5 (.value(C[3:0]));  // open: dp
  Hex_Digit_Display hex_digit_display_6 (.value(C[7:4]));  // open: dp
endmodule

module CPU (
  input  [7:0] Memory_In,
  input  [7:0] Input,
  input  Clock,
  output [7:0] Memory_Out,
  output [7:0] Memory_Address,
  output [7:0] Output,
  output Memory_RW
);

  wire and_1_out, data_path_1_z_out, not_1_out;
  wire [5:0] MIR_q_2, multiplexer_1_out, multiplexer_2_out, or_1_out;
  wire [17:0] MIR_q;
  wire [23:0] rom_1_data;

  Multiplexer #(.width(6), .disabled(0), .enable("false")) multiplexer_1 (
    .in0(multiplexer_2_out), .in1(or_1_out), .out(multiplexer_1_out), .sel(and_1_out));
  assign or_1_out = 6'b100000 | multiplexer_2_out;  // OR_Gate or_1, 6 bits wide
  Multiplexer #(.width(6), .disabled(0), .enable("false")) multiplexer_2 (
    .in0(Memory_Out[5:0]), .in1(MIR_q_2), .out(multiplexer_2_out), .sel(MIR_q[16]));
  ROM #(.addrWidth(6), .dataWidth(24)) rom_1 (.addr(multiplexer_1_out), .data(rom_1_data));  // open: sel
  and and_1 (and_1_out, data_path_1_z_out, MIR_q[17]);
  Register #(.width(24)) MIR (.D(rom_1_data), .Q({MIR_q_2, MIR_q}), .clk(Clock));  // open: en, clr
  not not_1 (not_1_out, MIR_q[8]);
  or or_2 (Memory_RW, not_1_out, MIR_q[1]);
  Data_Path data_path_1 (
    .Write_MAR(MIR_q[0]), .MBR_In(Memory_In), .Write_MBR(MIR_q[1]), .Switch_Input(Input),
    .B_Bus_Select(MIR_q[11:9]), .F(MIR_q[15:12]), .Clock(Clock), .MBR_Out(Memory_Out), .OUT_Out(Output),
    .Write_OUT(MIR_q[7]), .Write_Buf(MIR_q[6]), .Write_A(MIR_q[5]), .Write_B(MIR_q[4]), .Write_SP(MIR_q[3]),
    .Write_PC(MIR_q[2]), .MAR_Out(Memory_Address), .Z_Out(data_path_1_z_out), .Memory_RW(not_1_out));

  // Notes on the sheet:
  //   Virtual MPC
  //   High bit of Addr = 1
  //   contents of rom_1 (hex, n*v repeats v):
  //   3607 10000 11c20 11080 153607 11805 1d3607 11820 13020 11010 2d1040 14220 310000 393607 11808 411401
  //   451102 493508 11601 518409 551603 11820 5d3606 611801 651603 11820 6d3607 731000 11000 0 0 0 853606
  //   891801 8d1102 11701 13210 18020 18210 a11240 14010 a91040 15220 b11240 15010 b91040 bd1220 10010
  //   c53607 11810 10*0 11805
  //   Z
  //   JZ
  //   J
endmodule
